# Fritzing sketch weather (saved by Fritzing 0.9.5d)
breadboards: 2

parts:
  Raspberry_Pi_1 = Raspberry Pi 3 [part_number=RPI-3-V1.2]  # not connected
  J1 = T Cobbler Plus Cable
  Mod1 = KY-015 Temperature & Humidity Sensor Module [package="Breakout board"]
  M1 = DC Motor  # not connected
  M2 = DC Motor
  M3 = DC Motor
  M4 = DC Motor  # not connected
  Part1 = SparkFun Motor Driver TB6612FNG (v11) [part_number=ROB-14451]
  U1 = ENCODER-QUADRATURE [package=encoder-16mm-quad]  # not connected
  BAT1 = BC9VPC [package=bc9vpc]
  HC-SR04_Sensor_1 = HC-SR04 Ultrasonic Distance Sensor

nets:
  N1: J1.connector0, Mod1.S
  N2: J1.connector6, Mod1.Vin
  N3: J1.connector15, HC-SR04_Sensor_1.ECHO
  VCC: J1.connector16, Part1.VCC, Part1.STBY, HC-SR04_Sensor_1.VCC
  N4: J1.connector17, HC-SR04_Sensor_1.TRIG
  N5: J1.connector28, Part1.PWMA
  N6: J1.connector32, Part1.AIN2
  N7: J1.connector33, Mod1.-
  N8: J1.connector34, Part1.AIN1
  N9: J1.connector35, Part1.BIN1
  GND: J1.connector36, Part1.GND, Part1.VM, BAT1.V-, HC-SR04_Sensor_1.GND
  N10: J1.connector37, Part1.BIN2
  N11: J1.connector39, Part1.PWMB
  N12: M2.pin_1, Part1.B01
  N13: M2.pin_2, Part1.B02
  N14: M3.pin_1, Part1.A01
  N15: M3.pin_2, Part1.A02

custom parts:
  KY-015 Temperature & Humidity Sensor Module: KY-015 temperature and humidity sensor module, provides a low-latency serial interface to measure humidity and temperature.
  SparkFun Motor Driver TB6612FNG (v11): The TB6612FNG Motor Driver can control up to two DC motors at a constant current of 1.2A (3.2A peak). Two input signals (IN1 and IN2) can be used to control the motor in one of four function modes: CW, CCW, short-brake and stop. The two motor outputs (A and B) can be separately controlled, and the speed of each motor is controlled via a PWM input signal with a frequency up to 100kHz. The STBY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
