# Fritzing sketch updatedweather (saved by Fritzing 0.9.5d)
breadboards: 1

parts:
  Raspberry_Pi_1 = Raspberry Pi 3 [part_number=RPI-3-V1.2]
  VCC3 = 4 x AAA Battery Mount
  Part2 = SparkFun Motor Driver TB6612FNG (v11) [part_number=ROB-14451]
  HC-SR04_Sensor_1 = HC-SR04 Ultrasonic Distance Sensor
  Mod1 = KY-015 Temperature & Humidity Sensor Module [package="Breakout board"]
  M1 = DC Motor
  M2 = DC Motor
  M3 = DC Motor
  M4 = DC Motor
  R1 = Resistor [tolerance=±5% resistance=330 package=THT]
  R2 = Resistor [tolerance=±5% resistance=470 package=THT]

nets:
  3V3: Raspberry_Pi_1.3v3, Part2.VCC, Part2.STBY
  N1: Raspberry_Pi_1.GPIO4, Mod1.S
  N2: Raspberry_Pi_1.GPIO5, Part2.PWMA
  N3: Raspberry_Pi_1.GPIO13, Raspberry_Pi_1.GPIO26, Part2.AIN2
  N4: Raspberry_Pi_1.GPIO19, Part2.AIN1
  N5: Raspberry_Pi_1.GPIO21, Part2.PWMB
  N6: Raspberry_Pi_1.GPIO20, Part2.BIN2
  N7: Raspberry_Pi_1.GPIO16, Part2.BIN1
  N8: Raspberry_Pi_1.GPIO24, R1.Pin_1, R2.Pin_1
  N9: Raspberry_Pi_1.GPIO23, HC-SR04_Sensor_1.TRIG
  GND: Raspberry_Pi_1.GPIO15, Raspberry_Pi_1.GND, Part2.GND, HC-SR04_Sensor_1.GND, Mod1.-, R2.Pin_0
  5V: Raspberry_Pi_1.5V, HC-SR04_Sensor_1.VCC, Mod1.Vin
  N10: VCC3.+, Part2.VM
  N11: HC-SR04_Sensor_1.ECHO, R1.Pin_0
  N12: M1.pin_1, M3.pin_1
  N13: M1.pin_2, M3.pin_2
  N14: M2.pin_1, M4.pin_1
  N15: M2.pin_2, M4.pin_2

custom parts:
  SparkFun Motor Driver TB6612FNG (v11): The TB6612FNG Motor Driver can control up to two DC motors at a constant current of 1.2A (3.2A peak). Two input signals (IN1 and IN2) can be used to control the motor in one of four function modes: CW, CCW, short-brake and stop. The two motor outputs (A and B) can be separately controlled, and the speed of each motor is controlled via a PWM input signal with a frequency up to 100kHz. The STBY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
  KY-015 Temperature & Humidity Sensor Module: KY-015 temperature and humidity sensor module, provides a low-latency serial interface to measure humidity and temperature.
