# Fritzing sketch weather (saved by Fritzing 0.9.5d)
breadboards: 1

parts:
  Motor_Driver = SparkFun Motor Driver TB6612FNG (v11) [part_number=ROB-14451]
  Temperature_Sensor = KY-015 Temperature & Humidity Sensor Module [package="Breakout board"]
  M1 = DC Motor
  M2 = DC Motor
  M3 = DC Motor
  M4 = DC Motor
  C1 = Electrolytic Capacitor [capacitance=10µF package="100 mil [THT, electrolytic]"]
  R3 = Photocell (LDR) [package=THT]
  Raspberry_Pi_1 = Raspberry Pi 3 [part_number=RPI-3-V1.2]
  VCC1 = 4 x AAA Battery Mount

nets:
  N1: Motor_Driver.B01, M1.pin_1, M3.pin_1
  N2: Motor_Driver.B02, M1.pin_2, M3.pin_2
  N3: Motor_Driver.A02, M2.pin_2, M4.pin_2
  N4: Motor_Driver.A01, M2.pin_1, M4.pin_1
  3V3: Motor_Driver.VCC, Motor_Driver.STBY, Temperature_Sensor.S, R3.pin_0, Raspberry_Pi_1.3v3, Raspberry_Pi_1.3V3
  N5: Motor_Driver.VM, VCC1.+
  N6: Motor_Driver.PWMA, Raspberry_Pi_1.GPIO5
  N7: Motor_Driver.AIN2, Raspberry_Pi_1.GPIO13
  N8: Motor_Driver.AIN1, Raspberry_Pi_1.GPIO19
  N9: Motor_Driver.BIN1, Raspberry_Pi_1.GPIO16
  N10: Motor_Driver.BIN2, Raspberry_Pi_1.GPIO20
  N11: Motor_Driver.PWMB, Raspberry_Pi_1.GPIO21
  N12: Motor_Driver.GND, VCC1.-
  N13: Temperature_Sensor.Vin, Raspberry_Pi_1.GPIO4
  GND: Temperature_Sensor.-, C1.-
  N14: C1.+, R3.pin_1, Raspberry_Pi_1.GPIO17

custom parts:
  SparkFun Motor Driver TB6612FNG (v11): The TB6612FNG Motor Driver can control up to two DC motors at a constant current of 1.2A (3.2A peak). Two input signals (IN1 and IN2) can be used to control the motor in one of four function modes: CW, CCW, short-brake and stop. The two motor outputs (A and B) can be separately controlled, and the speed of each motor is controlled via a PWM input signal with a frequency up to 100kHz. The STBY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
  KY-015 Temperature & Humidity Sensor Module: KY-015 temperature and humidity sensor module, provides a low-latency serial interface to measure humidity and temperature.
